// Logisim project 5.circ as structural Verilog: 1 circuit, main circuit main
module main (
  input  [3:0] in_1,
  input  [3:0] in_2,
  input  CIN,
  input  in_4,
  input  in_5,
  input  in_6,
  input  in_7,
  input  in_8,
  input  in_9,
  input  in_10,
  input  in_11,
  input  in_12,
  input  in_13,
  input  in_14,
  input  in_15
);

  wire and_1_out, and_2_out, and_3_out, and_4_out, and_5_out, and_6_out, and_7_out, and_8_out, and_9_out,
       and_10_out, and_11_out, and_12_out, and_13_out, and_14_out, and_15_out, and_16_out, and_17_out,
       and_18_out, and_19_out, and_20_out, and_21_out, and_22_out, or_1_out, or_2_out, or_3_out, or_5_out,
       or_6_out, or_7_out, or_8_out, xor_1_out, xor_2_out, xor_3_out, xor_4_out, xor_5_out, xor_6_out,
       xor_7_out, xor_8_out;
  wire [0:0] or_4_out;
  wire [3:0] xor_9_out;

  xor xor_1 (xor_1_out, in_1[1], in_2[1]);
  and and_1 (and_1_out, in_1[1], in_2[1]);
  xor xor_2 (xor_2_out, in_1[2], in_2[2]);
  xor xor_3 (xor_3_out, in_1[3], in_2[3]);
  xor xor_4 (xor_4_out, in_1[0], in_2[0]);
  and and_2 (and_2_out, in_1[0], in_2[0]);
  and and_3 (and_3_out, in_1[2], in_2[2]);
  and and_4 (and_4_out, in_1[3], in_2[3]);
  xor xor_5 (xor_5_out, in_7, in_8);
  and and_5 (and_5_out, in_7, in_8);
  xor xor_6 (xor_6_out, in_10, in_11);
  and and_6 (and_6_out, in_10, in_11);
  xor xor_7 (xor_7_out, in_12, in_13);
  and and_7 (and_7_out, in_12, in_13);
  and and_8 (and_8_out, in_14, in_15);
  xor xor_8 (xor_8_out, in_14, in_15);
  xor xor_9 (xor_9_out[0], xor_4_out, CIN);
  and and_9 (and_9_out, xor_4_out, CIN);
  xor xor_10 (xor_9_out[1], xor_1_out, or_1_out);
  and and_10 (and_10_out, xor_1_out, or_1_out);
  xor xor_11 (xor_9_out[2], xor_2_out, or_2_out);
  and and_11 (and_11_out, xor_2_out, or_2_out);
  xor xor_12 (xor_9_out[3], xor_3_out, or_3_out);
  and and_12 (and_12_out, xor_3_out, or_3_out);
  and and_13 (and_13_out, xor_7_out, and_6_out);
  and and_14 (and_14_out, xor_8_out, and_7_out);
  and and_15 (and_15_out, xor_5_out, in_9);
  and and_16 (and_16_out, xor_6_out, xor_5_out, in_9);
  and and_17 (and_17_out, xor_6_out, xor_7_out, and_5_out);
  or or_1 (or_1_out, and_9_out, and_2_out);
  or or_2 (or_2_out, and_10_out, and_1_out);
  or or_3 (or_3_out, and_11_out, and_3_out);
  or or_4 (or_4_out[0], and_12_out, and_4_out);
  and and_18 (and_18_out, xor_6_out, and_5_out);
  and and_19 (and_19_out, xor_8_out, xor_7_out, and_6_out);
  and and_20 (and_20_out, xor_8_out, xor_7_out, xor_6_out, and_5_out);
  or or_5 (or_5_out, and_15_out, and_5_out);
  and and_21 (and_21_out, in_9, xor_7_out, xor_6_out, xor_5_out);
  Hex_Digit_Display hex_digit_display_1 (.value({in_6, in_5, in_4, or_4_out[0]}));  // open: dp
  or or_6 (or_6_out, and_18_out, and_6_out, and_16_out);
  or or_7 (or_7_out, and_13_out, and_17_out, and_21_out, and_7_out);
  and and_22 (and_22_out, in_9, xor_5_out, xor_6_out, xor_7_out, xor_6_out);
  or or_8 (or_8_out, and_14_out, and_19_out, and_20_out, and_22_out, and_8_out);
  Hex_Digit_Display hex_digit_display_2 (.value(xor_9_out));  // open: dp

  // Notes on the sheet:
  //   P2
  //   P3
  //   P0
  //   G0
  //   P1
  //   G1
  //   G2
  //   G3
  //   P0
  //   P0
  //   G0
  //   P1
  //   G1
  //   P2
  //   G2
  //   P3
  //   G3
  //   S0
  //   S1
  //   S2
  //   S3
  //   C1
  //   C2
  //   C3
  //   C4
  //   C1
  //   C2
  //   C3
  //   C4
endmodule
